# Fritzing sketch Sketch (saved by Fritzing 0.9.2b)
circuit board: 8.46667cm x 5.64444cm
breadboards: 1

parts:
  Part1 = Arduino Micro (Rev3)
  Grove1 = Grove OLED 128x96
  R1 = Trimmer Potentiometer [maximum_resistance=10kΩ package=THT]
  R2 = Resistor [tolerance=±5% resistance=220 package=THT]
  R3 = Temperature Sensor (Thermistor) [thermistor_type=NTC package=THT]
  R4 = Resistor [tolerance=±5% resistance=220 package="0805 [SMD]"]
  R5 = Resistor [tolerance=±5% resistance=220 package=THT]
  Q1 = NPN-Transistor [package="TO92 [THT]"]
  D1 = Rectifier Diode [part_number=1N4001 package="Melf DO-213 AB [SMD]"]
  U1 = RELAY [package=relay-jzc]

nets:
  N1: Part1.D2/SDA, Grove1.SDA
  N2: Part1.D3/SCL, Grove1.SCL
  N3: Part1.D8_PWM/A8, R2.Pin_0
  N4: Part1.D9_PWM/A9, R5.Pin_1
  GND: Part1.GND, Grove1.GND, R1.leg1, D1.cathode, U1.COIL1
  N5: Part1.A0, R1.wiper, R3.pin_0
  N6: Grove1.VCC, R4.Pin_0, Q1.E
  N7: R2.Pin_1, R3.pin_1
  N8: R4.Pin_1, R5.Pin_0, Q1.B
  N9: Q1.C, D1.anode, U1.COIL2
